# Fritzing sketch opdracht-2a (saved by Fritzing 1.0.2b)
breadboards: 1

parts:
  R1 = Resistor [tolerance=±5% power=0.25W resistance=220 package=THT]
  R2 = Resistor [tolerance=±5% power=0.25W resistance=220 package=THT]
  R3 = Resistor [tolerance=±5% power=0.25W resistance=220 package=THT]
  LED1 = smd LED [color="Red (633nm)" package="1206 [SMD]"]
  LED2 = smd LED [color="Red (633nm)" package="1206 [SMD]"]
  LED3 = smd LED [color="Red (633nm)" package="1206 [SMD]"]
  Part1 = Arduino Ethernet Shield (Rev3)

nets:
  N1: R1.Pin_0, Part1.PWM_D9
  N2: R1.Pin_1, LED3.anode
  N3: R2.Pin_0, Part1.PWM_D6
  N4: R2.Pin_1, LED2.anode
  N5: R3.Pin_0, Part1.PWM_D5
  N6: R3.Pin_1, LED1.anode
  N7: LED1.cathode, LED2.cathode, LED3.cathode, Part1.GND
