# Fritzing sketch opdracht-3 (saved by Fritzing 1.0.2b)
breadboards: 1

parts:
  R1 = Resistor [tolerance=±5% power=0.25W resistance=220 package=THT]
  LED3 = smd LED [color="Red (633nm)" package="1206 [SMD]"]
  Part1 = Arduino Ethernet Shield (Rev3)
  R2 = Resistor [tolerance=±5% power=0.25W resistance=220 package=THT]
  LED4 = smd LED [color="Red (633nm)" package="1206 [SMD]"]

nets:
  N1: R1.Pin_0, Part1.SPI/D13
  N2: R1.Pin_1, LED3.anode
  N3: LED3.cathode, Part1.GND
  N4: Part1.PWM_D5, R2.Pin_0
  N5: R2.Pin_1, LED4.cathode

// code stored in the sketch: opdracht-1.ino
void setup() {
  // put your setup code here, to run once:
  pinMode(5, OUTPUT);
  pinMode(6, OUTPUT);
  pinMode(9, OUTPUT);
}


void loop() {
  // put your main code here, to run repeatedly:
  digitalWrite(9, LOW);
  digitalWrite(5, HIGH);
  delay(1000);
  digitalWrite(6, HIGH);
  delay(1000);
  digitalWrite(5, LOW);
  digitalWrite(6, LOW);
  digitalWrite(9, HIGH);
  delay(1000);
}

// code stored in the sketch: opdracht-2a.ino
void setup() {
  // put your setup code here, to run once:
  pinMode(5, OUTPUT);
  pinMode(6, OUTPUT);
  pinMode(9, OUTPUT);
}


void loop() {
  // put your main code here, to run repeatedly:
  digitalWrite(9, LOW);
  digitalWrite(5, HIGH);
  delay(1000);
  digitalWrite(6, HIGH);
  delay(1000);
  digitalWrite(5, LOW);
  digitalWrite(6, LOW);
  digitalWrite(9, HIGH);
  delay(1000);
}
